# Fritzing sketch MIDI_Accordion (saved by Fritzing 0.9.3b)
stripboards: 3

parts:
  R73 = Resistor [tolerance=±5% resistance=1k package="0603 [SMD]"]
  R65 = Resistor [tolerance=±5% resistance=270 package="0603 [SMD]"]
  T8 = TRANSISTOR_NPN [part_number=2N2222A package=to-92]
  U65 = CNZ1120 [part_number=ITR-9608 package=cnz1120]
  Mega = Arduino Mega 2560 (Rev3)
  BMP180 = Barometric Pressure Sensor - BMP085 Breakout
  HC-05 = Bluetooth HC-05 Macho
  U5 = CNZ1120 [part_number=ITR-9608 package=cnz1120]
  R5 = Resistor [tolerance=±5% resistance=270 package="0603 [SMD]"]
  U13 = CNZ1120 [part_number=ITR-9608 package=cnz1120]
  R13 = Resistor [tolerance=±5% resistance=270 package="0603 [SMD]"]
  U21 = CNZ1120 [part_number=ITR-9608 package=cnz1120]
  R21 = Resistor [tolerance=±5% resistance=270 package="0603 [SMD]"]
  U29 = CNZ1120 [part_number=ITR-9608 package=cnz1120]
  R29 = Resistor [tolerance=±5% resistance=270 package="0603 [SMD]"]
  U37 = CNZ1120 [part_number=ITR-9608 package=cnz1120]
  R37 = Resistor [tolerance=±5% resistance=270 package="0603 [SMD]"]
  U45 = CNZ1120 [part_number=ITR-9608 package=cnz1120]
  R45 = Resistor [tolerance=±5% resistance=270 package="0603 [SMD]"]
  U53 = CNZ1120 [part_number=ITR-9608 package=cnz1120]
  R53 = Resistor [tolerance=±5% resistance=270 package="0603 [SMD]"]
  U61 = CNZ1120 [part_number=ITR-9608 package=cnz1120]
  R61 = Resistor [tolerance=±5% resistance=270 package="0603 [SMD]"]
  U4 = CNZ1120 [part_number=ITR-9608 package=cnz1120]
  R4 = Resistor [tolerance=±5% resistance=270 package="0603 [SMD]"]
  U12 = CNZ1120 [part_number=ITR-9608 package=cnz1120]
  R12 = Resistor [tolerance=±5% resistance=270 package="0603 [SMD]"]
  U20 = CNZ1120 [part_number=ITR-9608 package=cnz1120]
  R20 = Resistor [tolerance=±5% resistance=270 package="0603 [SMD]"]
  U28 = CNZ1120 [part_number=ITR-9608 package=cnz1120]
  R28 = Resistor [tolerance=±5% resistance=270 package="0603 [SMD]"]
  U36 = CNZ1120 [part_number=ITR-9608 package=cnz1120]
  R36 = Resistor [tolerance=±5% resistance=270 package="0603 [SMD]"]
  U44 = CNZ1120 [part_number=ITR-9608 package=cnz1120]
  R44 = Resistor [tolerance=±5% resistance=270 package="0603 [SMD]"]
  U52 = CNZ1120 [part_number=ITR-9608 package=cnz1120]
  R52 = Resistor [tolerance=±5% resistance=270 package="0603 [SMD]"]
  U60 = CNZ1120 [part_number=ITR-9608 package=cnz1120]
  R60 = Resistor [tolerance=±5% resistance=270 package="0603 [SMD]"]
  U59 = CNZ1120 [part_number=ITR-9608 package=cnz1120]
  U43 = CNZ1120 [part_number=ITR-9608 package=cnz1120]
  U3 = CNZ1120 [part_number=ITR-9608 package=cnz1120]
  U51 = CNZ1120 [part_number=ITR-9608 package=cnz1120]
  U35 = CNZ1120 [part_number=ITR-9608 package=cnz1120]
  U11 = CNZ1120 [part_number=ITR-9608 package=cnz1120]
  U19 = CNZ1120 [part_number=ITR-9608 package=cnz1120]
  U27 = CNZ1120 [part_number=ITR-9608 package=cnz1120]
  R19 = Resistor [tolerance=±5% resistance=270 package="0603 [SMD]"]
  R27 = Resistor [tolerance=±5% resistance=270 package="0603 [SMD]"]
  R43 = Resistor [tolerance=±5% resistance=270 package="0603 [SMD]"]
  R3 = Resistor [tolerance=±5% resistance=270 package="0603 [SMD]"]
  R11 = Resistor [tolerance=±5% resistance=270 package="0603 [SMD]"]
  R59 = Resistor [tolerance=±5% resistance=270 package="0603 [SMD]"]
  R35 = Resistor [tolerance=±5% resistance=270 package="0603 [SMD]"]
  R51 = Resistor [tolerance=±5% resistance=270 package="0603 [SMD]"]
  U58 = CNZ1120 [part_number=ITR-9608 package=cnz1120]
  U42 = CNZ1120 [part_number=ITR-9608 package=cnz1120]
  U2 = CNZ1120 [part_number=ITR-9608 package=cnz1120]
  U50 = CNZ1120 [part_number=ITR-9608 package=cnz1120]
  U34 = CNZ1120 [part_number=ITR-9608 package=cnz1120]
  U10 = CNZ1120 [part_number=ITR-9608 package=cnz1120]
  U18 = CNZ1120 [part_number=ITR-9608 package=cnz1120]
  U26 = CNZ1120 [part_number=ITR-9608 package=cnz1120]
  R18 = Resistor [tolerance=±5% resistance=270 package="0603 [SMD]"]
  R26 = Resistor [tolerance=±5% resistance=270 package="0603 [SMD]"]
  R42 = Resistor [tolerance=±5% resistance=270 package="0603 [SMD]"]
  R2 = Resistor [tolerance=±5% resistance=270 package="0603 [SMD]"]
  R10 = Resistor [tolerance=±5% resistance=270 package="0603 [SMD]"]
  R58 = Resistor [tolerance=±5% resistance=270 package="0603 [SMD]"]
  R34 = Resistor [tolerance=±5% resistance=270 package="0603 [SMD]"]
  R50 = Resistor [tolerance=±5% resistance=270 package="0603 [SMD]"]
  U38 = CNZ1120 [part_number=ITR-9608 package=cnz1120]
  U46 = CNZ1120 [part_number=ITR-9608 package=cnz1120]
  U30 = CNZ1120 [part_number=ITR-9608 package=cnz1120]
  U54 = CNZ1120 [part_number=ITR-9608 package=cnz1120]
  U62 = CNZ1120 [part_number=ITR-9608 package=cnz1120]
  U6 = CNZ1120 [part_number=ITR-9608 package=cnz1120]
  U14 = CNZ1120 [part_number=ITR-9608 package=cnz1120]
  U22 = CNZ1120 [part_number=ITR-9608 package=cnz1120]
  R46 = Resistor [tolerance=±5% resistance=270 package="0603 [SMD]"]
  R62 = Resistor [tolerance=±5% resistance=270 package="0603 [SMD]"]
  R22 = Resistor [tolerance=±5% resistance=270 package="0603 [SMD]"]
  R6 = Resistor [tolerance=±5% resistance=270 package="0603 [SMD]"]
  R54 = Resistor [tolerance=±5% resistance=270 package="0603 [SMD]"]
  R14 = Resistor [tolerance=±5% resistance=270 package="0603 [SMD]"]
  R30 = Resistor [tolerance=±5% resistance=270 package="0603 [SMD]"]
  R38 = Resistor [tolerance=±5% resistance=270 package="0603 [SMD]"]
  U39 = CNZ1120 [part_number=ITR-9608 package=cnz1120]
  U47 = CNZ1120 [part_number=ITR-9608 package=cnz1120]
  U31 = CNZ1120 [part_number=ITR-9608 package=cnz1120]
  U55 = CNZ1120 [part_number=ITR-9608 package=cnz1120]
  U63 = CNZ1120 [part_number=ITR-9608 package=cnz1120]
  U7 = CNZ1120 [part_number=ITR-9608 package=cnz1120]
  U15 = CNZ1120 [part_number=ITR-9608 package=cnz1120]
  R47 = Resistor [tolerance=±5% resistance=270 package="0603 [SMD]"]
  R63 = Resistor [tolerance=±5% resistance=270 package="0603 [SMD]"]
  R23 = Resistor [tolerance=±5% resistance=270 package="0603 [SMD]"]
  R7 = Resistor [tolerance=±5% resistance=270 package="0603 [SMD]"]
  R55 = Resistor [tolerance=±5% resistance=270 package="0603 [SMD]"]
  R15 = Resistor [tolerance=±5% resistance=270 package="0603 [SMD]"]
  R31 = Resistor [tolerance=±5% resistance=270 package="0603 [SMD]"]
  R39 = Resistor [tolerance=±5% resistance=270 package="0603 [SMD]"]
  U40 = CNZ1120 [part_number=ITR-9608 package=cnz1120]
  U64 = CNZ1120 [part_number=ITR-9608 package=cnz1120]
  U56 = CNZ1120 [part_number=ITR-9608 package=cnz1120]
  U48 = CNZ1120 [part_number=ITR-9608 package=cnz1120]
  U32 = CNZ1120 [part_number=ITR-9608 package=cnz1120]
  U24 = CNZ1120 [part_number=ITR-9608 package=cnz1120]
  U8 = CNZ1120 [part_number=ITR-9608 package=cnz1120]
  U16 = CNZ1120 [part_number=ITR-9608 package=cnz1120]
  R48 = Resistor [tolerance=±5% resistance=270 package="0603 [SMD]"]
  R64 = Resistor [tolerance=±5% resistance=270 package="0603 [SMD]"]
  R24 = Resistor [tolerance=±5% resistance=270 package="0603 [SMD]"]
  R56 = Resistor [tolerance=±5% resistance=270 package="0603 [SMD]"]
  R32 = Resistor [tolerance=±5% resistance=270 package="0603 [SMD]"]
  R16 = Resistor [tolerance=±5% resistance=270 package="0603 [SMD]"]
  R8 = Resistor [tolerance=±5% resistance=270 package="0603 [SMD]"]
  R40 = Resistor [tolerance=±5% resistance=270 package="0603 [SMD]"]
  T7 = TRANSISTOR_NPN [part_number=2N2222A package=to-92]
  R72 = Resistor [tolerance=±5% resistance=1k package="0603 [SMD]"]
  T6 = TRANSISTOR_NPN [part_number=2N2222A package=to-92]
  R71 = Resistor [tolerance=±5% resistance=1k package="0603 [SMD]"]
  T5 = TRANSISTOR_NPN [part_number=2N2222A package=to-92]
  R70 = Resistor [tolerance=±5% resistance=1k package="0603 [SMD]"]
  T1 = TRANSISTOR_NPN [part_number=2N2222A package=to-92]
  R66 = Resistor [tolerance=±5% resistance=1k package="0603 [SMD]"]
  T2 = TRANSISTOR_NPN [part_number=2N2222A package=to-92]
  R67 = Resistor [tolerance=±5% resistance=1k package="0603 [SMD]"]
  T3 = TRANSISTOR_NPN [part_number=2N2222A package=to-92]
  R68 = Resistor [tolerance=±5% resistance=1k package="0603 [SMD]"]
  T4 = TRANSISTOR_NPN [part_number=2N2222A package=to-92]
  R69 = Resistor [tolerance=±5% resistance=1k package="0603 [SMD]"]
  U41 = CNZ1120 [part_number=ITR-9608 package=cnz1120]
  U17 = CNZ1120 [part_number=ITR-9608 package=cnz1120]
  U57 = CNZ1120 [part_number=ITR-9608 package=cnz1120]
  U1 = CNZ1120 [part_number=ITR-9608 package=cnz1120]
  U9 = CNZ1120 [part_number=ITR-9608 package=cnz1120]
  U33 = CNZ1120 [part_number=ITR-9608 package=cnz1120]
  U49 = CNZ1120 [part_number=ITR-9608 package=cnz1120]
  U25 = CNZ1120 [part_number=ITR-9608 package=cnz1120]
  R33 = Resistor [tolerance=±5% resistance=270 package="0603 [SMD]"]
  R17 = Resistor [tolerance=±5% resistance=270 package="0603 [SMD]"]
  R1 = Resistor [tolerance=±5% resistance=270 package="0603 [SMD]"]
  R57 = Resistor [tolerance=±5% resistance=270 package="0603 [SMD]"]
  R9 = Resistor [tolerance=±5% resistance=270 package="0603 [SMD]"]
  R25 = Resistor [tolerance=±5% resistance=270 package="0603 [SMD]"]
  R41 = Resistor [tolerance=±5% resistance=270 package="0603 [SMD]"]
  R49 = Resistor [tolerance=±5% resistance=270 package="0603 [SMD]"]
  To_Port_F = shrouded pin header, 8 pins [form="♂ (shrouded male)"]
  Port_F = shrouded pin header, 8 pins [form="♂ (shrouded male)"]
  R74 = Resistor [tolerance=±5% resistance=1k package=THT]
  R75 = Resistor [tolerance=±5% resistance=2.2k package=THT]
  U23 = CNZ1120 [part_number=ITR-9608 package=cnz1120]
  To_Port_K = shrouded pin header, 8 pins [form="♂ (shrouded male)"]
  Port_K = shrouded pin header, 8 pins [form="♂ (shrouded male)"]
  Port_A = shrouded pin header, 8 pins [form="♂ (shrouded male)"]
  To_Port_A = shrouded pin header, 8 pins [form="♂ (shrouded male)"]
  JOY1 = Trimmer Potentiometer [maximum_resistance=10kΩ package=THT]

nets (from the schematic view):
  N1: R73.Pin_0, T8.B
  N2: R73.Pin_1, Mega.D53
  N3: R65.Pin_0, To_Port_A.pin1
  N4: R65.Pin_1, U65.1
  GND: T8.E, U65.2, U65.4, Mega.GND, BMP180.GND, HC-05.GND, U5.4, U13.4, U21.4, U29.4, U37.4, U45.4, U53.4, U61.4, U4.4, U12.4, U20.4, U28.4, U36.4, U44.4, U52.4, U60.4, U59.4, U43.4, U3.4, U51.4, U35.4, U11.4, U19.4, U27.4, U58.4, U42.4, U2.4, U50.4, U34.4, U10.4, U18.4, U26.4, U38.4, U46.4, U30.4, U54.4, U62.4, U6.4, U14.4, U22.4, U39.4, U47.4, U31.4, U55.4, U63.4, U7.4, U15.4, U40.4, U64.4, U56.4, U48.4, U32.4, U24.4, U8.4, U16.4, T7.E, T6.E, T5.E, T1.E, T2.E, T3.E, T4.E, U41.4, U17.4, U57.4, U1.4, U9.4, U33.4, U49.4, U25.4, R75.Pin_0, U23.4, JOY1.leg1
  N5: T8.C, U5.2, U4.2, U3.2, U2.2, U6.2, U7.2, U8.2, U1.2
  N6: U65.3, Mega.A15, U64.3
  N7: Mega.A0, JOY1.wiper
  N8: Mega.D21/SCL, Mega.SCL, BMP180.SCL
  N9: Mega.D20/SDA, Mega.SDA, BMP180.SDA
  N10: Mega.D19/RX1, HC-05.RXD
  N11: Mega.D18/TX1, R74.Pin_0
  3.3V: Mega.3V3, BMP180.VCC, HC-05.VCC
  5V: Mega.5V, R5.Pin_0, R13.Pin_0, R21.Pin_0, R29.Pin_0, R37.Pin_0, R45.Pin_0, R53.Pin_0, R61.Pin_0, R4.Pin_0, R12.Pin_0, R20.Pin_0, R28.Pin_0, R36.Pin_0, R44.Pin_0, R52.Pin_0, R60.Pin_0, R19.Pin_0, R27.Pin_0, R43.Pin_0, R3.Pin_0, R11.Pin_0, R59.Pin_0, R35.Pin_0, R51.Pin_0, R18.Pin_0, R26.Pin_0, R42.Pin_0, R2.Pin_0, R10.Pin_0, R58.Pin_0, R34.Pin_0, R50.Pin_0, R46.Pin_0, R62.Pin_0, R22.Pin_0, R6.Pin_0, R54.Pin_0, R14.Pin_0, R30.Pin_0, R38.Pin_0, R47.Pin_0, R63.Pin_0, R23.Pin_0, R7.Pin_0, R55.Pin_0, R15.Pin_0, R31.Pin_0, R39.Pin_0, R48.Pin_0, R64.Pin_0, R24.Pin_0, R56.Pin_0, R32.Pin_0, R16.Pin_0, R8.Pin_0, R40.Pin_0, R33.Pin_0, R17.Pin_0, R1.Pin_0, R57.Pin_0, R9.Pin_0, R25.Pin_0, R41.Pin_0, R49.Pin_0, JOY1.leg2
  N12: Mega.D22, Port_A.pin1
  N13: Mega.D23, Port_A.pin2
  N14: Mega.D24, Port_A.pin3
  N15: Mega.D25, Port_A.pin4
  N16: Mega.D26, Port_A.pin5
  N17: Mega.D27, Port_A.pin6
  N18: Mega.D28, Port_A.pin7
  N19: Mega.D29, Port_A.pin8
  N20: Mega.D30, Port_K.pin1
  N21: Mega.D31, Port_K.pin2
  N22: Mega.D32, Port_K.pin3
  N23: Mega.D33, Port_K.pin4
  N24: Mega.D34, Port_K.pin5
  N25: Mega.D35, Port_K.pin6
  N26: Mega.D36, Port_K.pin7
  N27: Mega.D37, Port_K.pin8
  N28: Mega.D42, Port_F.pin1
  N29: Mega.D43, Port_F.pin2
  N30: Mega.D44, Port_F.pin3
  N31: Mega.D45, Port_F.pin4
  N32: Mega.D46, Port_F.pin5
  N33: Mega.D47, Port_F.pin6
  N34: Mega.D48, Port_F.pin7
  N35: Mega.D49, Port_F.pin8
  N36: Mega.D50, R71.Pin_1
  N37: Mega.D52, R72.Pin_1
  N38: HC-05.TXD, R74.Pin_1, R75.Pin_1
  N39: U5.1, R5.Pin_1
  N40: U5.3, U13.3, U21.3, To_Port_F.pin5
  N41: U13.1, R13.Pin_1
  N42: U13.2, U12.2, U11.2, U10.2, U14.2, U15.2, U16.2, T7.C, U9.2
  N43: U21.1, R21.Pin_1
  N44: U21.2, U20.2, U19.2, U18.2, U22.2, U24.2, T6.C, U17.2, U23.2
  N45: U29.1, R29.Pin_1
  N46: U29.2, U28.2, U27.2, U26.2, U30.2
  N47: U29.3, U37.3, U45.3, U53.3, U61.3, To_Port_K.pin5
  N48: U37.1, R37.Pin_1
  N49: U37.2, U36.2, U35.2, U34.2, U38.2, U39.2, U40.2, T4.C, U33.2
  N50: U45.1, R45.Pin_1
  N51: U45.2, U44.2, U43.2, U42.2, U46.2, U47.2, U48.2, T3.C, U41.2
  N52: U53.1, R53.Pin_1
  N53: U53.2, U52.2, U51.2, U50.2, U54.2, U55.2, U56.2, T2.C, U49.2
  N54: U61.1, R61.Pin_1
  N55: U61.2, U60.2, U59.2, U58.2, U62.2, U63.2, U64.2, T1.C, U57.2
  N56: U4.1, R4.Pin_1
  N57: U4.3, U12.3, U20.3, To_Port_F.pin4
  N58: U12.1, R12.Pin_1
  N59: U20.1, R20.Pin_1
  N60: U28.1, R28.Pin_1
  N61: U28.3, U36.3, U44.3, U52.3, U60.3, To_Port_K.pin4
  N62: U36.1, R36.Pin_1
  N63: U44.1, R44.Pin_1
  N64: U52.1, R52.Pin_1
  N65: U60.1, R60.Pin_1
  N66: U59.1, R59.Pin_1
  N67: U59.3, U43.3, U51.3, U35.3, U27.3, To_Port_K.pin3
  N68: U43.1, R43.Pin_1
  N69: U3.1, R3.Pin_1
  N70: U3.3, U11.3, U19.3, To_Port_F.pin3
  N71: U51.1, R51.Pin_1
  N72: U35.1, R35.Pin_1
  N73: U11.1, R11.Pin_1
  N74: U19.1, R19.Pin_1
  N75: U27.1, R27.Pin_1
  N76: U58.1, R58.Pin_1
  N77: U58.3, U42.3, U50.3, U34.3, U26.3, To_Port_K.pin2
  N78: U42.1, R42.Pin_1
  N79: U2.1, R2.Pin_1
  N80: U2.3, U10.3, U18.3, To_Port_F.pin2
  N81: U50.1, R50.Pin_1
  N82: U34.1, R34.Pin_1
  N83: U10.1, R10.Pin_1
  N84: U18.1, R18.Pin_1
  N85: U26.1, R26.Pin_1
  N86: U38.1, R38.Pin_1
  N87: U38.3, U46.3, U30.3, U54.3, U62.3, To_Port_K.pin6
  N88: U46.1, R46.Pin_1
  N89: U30.1, R30.Pin_1
  N90: U54.1, R54.Pin_1
  N91: U62.1, R62.Pin_1
  N92: U6.1, R6.Pin_1
  N93: U6.3, U14.3, U22.3, To_Port_F.pin6
  N94: U14.1, R14.Pin_1
  N95: U22.1, R22.Pin_1
  N96: U39.1, R39.Pin_1
  N97: U39.3, U47.3, U31.3, U55.3, U63.3, To_Port_K.pin7
  N98: U47.1, R47.Pin_1
  N99: U31.1, R31.Pin_1
  N100: U31.2, U32.2, T5.C, U25.2
  N101: U55.1, R55.Pin_1
  N102: U63.1, R63.Pin_1
  N103: U7.1, R7.Pin_1
  N104: U7.3, U15.3, To_Port_F.pin7, U23.3
  N105: U15.1, R15.Pin_1
  N106: R23.Pin_1, U23.1
  N107: U40.1, R40.Pin_1
  N108: U40.3, U56.3, U48.3, U32.3, To_Port_K.pin8
  N109: U64.1, R64.Pin_1
  N110: U56.1, R56.Pin_1
  N111: U48.1, R48.Pin_1
  N112: U32.1, R32.Pin_1
  N113: U24.1, R24.Pin_1
  N114: U24.3, U8.3, U16.3, To_Port_F.pin8
  N115: U8.1, R8.Pin_1
  N116: U16.1, R16.Pin_1
  N117: T7.B, R72.Pin_0
  N118: T6.B, R71.Pin_0
  N119: T5.B, R70.Pin_0
  N120: R70.Pin_1, To_Port_A.pin2
  N121: T1.B, R66.Pin_0
  N122: R66.Pin_1, To_Port_A.pin3
  N123: T2.B, R67.Pin_0
  N124: R67.Pin_1, To_Port_A.pin5
  N125: T3.B, R68.Pin_0
  N126: R68.Pin_1, To_Port_A.pin6
  N127: T4.B, R69.Pin_0
  N128: R69.Pin_1, To_Port_A.pin4
  N129: U41.1, R41.Pin_1
  N130: U41.3, U57.3, U33.3, U49.3, U25.3, To_Port_K.pin1
  N131: U17.1, R17.Pin_1
  N132: U17.3, U1.3, U9.3, To_Port_F.pin1
  N133: U57.1, R57.Pin_1
  N134: U1.1, R1.Pin_1
  N135: U9.1, R9.Pin_1
  N136: U33.1, R33.Pin_1
  N137: U49.1, R49.Pin_1
  N138: U25.1, R25.Pin_1

notes:
  There are 8 of these opto-interruptor circuit boards in my final project.
  3 of them are on the bass side, cut in half, and use D50, 52, and 53 (formerly D10-12) for the diodes and D30-37 (formerly A8-15) for the transistors.
  5 of them are on the treble side and use D23-27 (formerly D2-6) for the diodes and D42-49 (formerly A0-7) for the transistors. One of those 5 boards has a ninth opto-interruptor that uses D22 (formerly D7).
  See original project photos for details.

// code stored in the sketch: BMP_180.ino
#include <SFE_BMP180.h>
#include <Wire.h>

SFE_BMP180 bmp_180;

double Temp, P;
int tempStatus;
int pressureStatus;
double Calib_Pressure;

void init_BMP() {
  #ifdef DEBUG
    Serial.println("REBOOTING BMP180");
  #endif
  // Initialize and calibrate the sensor
  if (bmp_180.begin())
  {
    //get an average reading
    for (int i=0; i<32; i++){
      Calib_Pressure += readPressure();
      delayMicroseconds(500);
    }
    Calib_Pressure = Calib_Pressure/32;
  }
  else //something went wrong - this is usually a connection problem
  {
    #ifdef DEBUG
      Serial.println("BMP180 init fail\n\n");
    #endif
    while(1); // Pause forever.
  }
  #ifdef DEBUG
    Serial.println("BMP180 init success");
  #endif
  reset_flags();
}

//This is only used to calibrate the BMP on startup because it takes about 12ms
double readPressure() {
  //We need to read the temperature every time because 
  //wind affects it, which in turn affects the pressure
  tempStatus = bmp_180.startTemperature();
  if (tempStatus != 0)
  {
    delay(tempStatus);// Wait for the measurement to complete:

    // Retrieve the completed temperature measurement:
    tempStatus = bmp_180.getTemperature(Temp);//sets Temp 
    if (tempStatus != 0)
    {
      // Start a pressure measurement:
      pressureStatus = bmp_180.startPressure(0);//Passing in 0 for speed
      if (pressureStatus != 0)
      {
        delay(pressureStatus);// Wait for the measurement to complete:
    
        // Retrieve the completed pressure measurement using the given temp:
        pressureStatus = bmp_180.getPressure(P,Temp);//sets P to pressure (in millibars)
        if (pressureStatus == 0) {
          #ifdef DEBUG
            Serial.println("error retrieving pressure measurement\n");
          #endif
        }
      }
      else {
        #ifdef DEBUG
          Serial.println("error starting pressure measurement\n");
        #endif
      }
    }
    else {
      #ifdef DEBUG
        Serial.println("error retrieving temperature measurement\n");
      #endif
    }
  }
  else {
    #ifdef DEBUG
      Serial.println("error starting temperature measurement\n");
    #endif
  }
  
  return P*100;//converting from millibars to pascals
}

int temp_wait_ms = 0; 
int pressure_wait_ms = 0;
unsigned long temp_init_ms = 0; 
unsigned long temp_final_ms = 0; 
unsigned long pressure_init_ms = 0;
unsigned long pressure_final_ms = 0;

bool need_temp_reading = true;
bool temp_started = false;
bool temp_ready = false;
bool pressure_started = false;
bool pressure_ready = false;

void reset_flags(){
  need_temp_reading = true;
  temp_started = false;
  temp_ready = false;
  pressure_started = false;
  pressure_ready = false;
  temp_wait_ms = 0; 
  pressure_wait_ms = 0;
  temp_init_ms = 0; 
  temp_final_ms = 0; 
  pressure_init_ms = 0;
  pressure_final_ms = 0;
}

/* If we're entering this function, we're in one of the following states:
*  1 - We just entered and need a temp reading
*  2 - We're waiting for temp reading but it's not ready yet
*  3 - Temp reading is ready so we can start pressure reading
*  4 - We're waiting for pressure reading but it's not ready yet
*  5 - pressure reading is ready and we can get our new expression
*/
int get_expression(int prev_expression) {
  int expression = prev_expression;

  if(need_temp_reading) {//States 1-3
    if(temp_started && !temp_ready){//2 - We're waiting for temp reading but it's not ready yet
      temp_final_ms = millis();
      temp_wait_ms = temp_wait_ms + (temp_final_ms - temp_init_ms);
      temp_init_ms = millis();
      if(temp_wait_ms > tempStatus){
        temp_ready = true;
      }
    }
    if(!temp_started){//1 - We just entered and need a temp reading
      temp_init_ms = millis();
      tempStatus = bmp_180.startTemperature();
      temp_started = true;
    }
    if(temp_ready){//3 - Temp reading is ready so we can start pressure reading
      tempStatus = bmp_180.getTemperature(Temp);
      need_temp_reading = false;
      pressure_init_ms = millis();
      pressureStatus = bmp_180.startPressure(0);
      pressure_started = true;
    }
  }
  else if(pressure_started) {//States 4-5
    if(!pressure_ready) {//4 - We're waiting for pressure reading but it's not ready yet
      pressure_final_ms = millis();
      pressure_wait_ms = pressure_wait_ms + (pressure_final_ms - pressure_init_ms);
      pressure_init_ms = millis();
      if(pressure_wait_ms > tempStatus){
        pressure_ready = true;
      }
    }
    if(pressure_ready) {//5 - pressure reading is ready and we can get our new expression
      pressureStatus = bmp_180.getPressure(P,Temp);
      expression = get_expression_from_pressure(P*100);//converting millibars to pascals
      reset_flags();
    }
  }

  return expression;
}

//Minimum amount of pressure change required to cause a change in volume.
int pressure_low_limit = 15;
//I decided to use a non-zero value for the minimum velocity.
//Although being able to sound without moving is not realistic, 
//it helps to compensate for having to push the bellows harder.
//Also, working with a smaller range allows for smoother dynamics
//because larger changes in pressure will cause smaller changes in volume.
int min_velocity = 55;

//Algorithm used to map pressure deltas into MIDI velocity
//Tweaks may need to be made for each accordion based on where the BMP_180 was placed 
//and how much air flows through the accordion when keys are pressed.
int get_expression_from_pressure(double Pressure) {
  int expression;
  float Pressure_Delta = abs(Pressure - Calib_Pressure);
  #ifdef BLUETOOTH
    //Uncomment this while sending MIDI data via Bluetooth to get
    //pressure delta output on the serial port while playing music.
//    if (Pressure_Delta > pressure_low_limit){ 
//      Serial.print("Pressure_Delta: ");
//      Serial.println(int(Pressure_Delta));
//    }
  #endif

  //I derived this formula from a graphing calculator (https://www.desmos.com/) 
  //I started with a cubic function: y=m(x-c)^3+nx+b
  //I set the constants until the contour fell in line with 
  //the expected pressure range and MIDI velocity output (0<x<250,0<y<127).
  //From there I tweaked values and play tested them until
  //I got something that sounded and felt right.
  //This function may need to be tweaked for different accordions and playing styles.
  expression = int(0.000014*pow(Pressure_Delta-162,3) + 0.01*Pressure_Delta)+99;

  //If the pressure delta is below the defined limit, set it to the minimum velocity.
  //This works best when the mapping function hits the coordinate where
  //x = pressure_low_limit and y = min_velocity
  if (Pressure_Delta < pressure_low_limit){ 
    expression = min_velocity;
  }
  if (expression > 127){
    expression = 127;
  }

  return expression;
}

// code stored in the sketch: Interruptor_4_Uno.ino
/* 
* 2x2 matrix of Interruptors
* At this point most of this code is pulled directly from AccordionMega's code.
*/

int ANALOG_ROW1 = 2;//00000100
//int ANALOG_ROW2 = 3;
char DIGITAL_COLUMNS[] = { 9, 10 };

//Note: in this example we're only using two bits from each byte
int KeysStatus[] = {  
  B0000000,
  B0000000
};

//this is the value of all pins from the analog port (7 and 6 don't exist on UNO)
//B00000000
//B76543210
byte reg_values = 0;

void setup()
{
    Serial.begin(9600);
    //Digital pins start turned off
    for (int i=0; i<sizeof(DIGITAL_COLUMNS);i++){ 
        pinMode(DIGITAL_COLUMNS[i],OUTPUT);
        digitalWrite(DIGITAL_COLUMNS[i], LOW);
    }

    //PortC as input 
    DDRC = B00000000;
    //Turn on pullup resistors
    PORTC = B11111111;
}

void loop()
{
  for (int i=0; i<sizeof(DIGITAL_COLUMNS);i++){ 
    //I wonder if we can replace this with direct port write for speed?
    digitalWrite(DIGITAL_COLUMNS[i], HIGH);
    delayMicroseconds(7000);//TODO - play around with this number a bit

    //delay(500);
    
    //PINB = 8-13 (14/15 don't work), PINC = analog 0-5 (6/7 don't work), PIND = 0-7
    reg_values = ~PINC;
//    Serial.println(" ");
//    Serial.print(" Previous Values for group ");
//    Serial.print(i);
//    Serial.print(": ");
//    Serial.println(KeysStatus[i], BIN);
//    Serial.print(" Values Read: ");
//    Serial.println(reg_values, BIN);
    
    
    digitalWrite(DIGITAL_COLUMNS[i], LOW);

    if (reg_values != KeysStatus[i]){
      if (reg_values > KeysStatus[i]){             
        check_key(reg_values ^ KeysStatus[i],i,true);  //sending modified bits only
      }
      else {
        check_key(reg_values ^ KeysStatus[i],i,false); //sending modified bits only
      }           
    }
  }
}

void check_key(int reg, int group, boolean up){
   // saving 4 iterations, dividing byte by 2
   if (reg & 0xF0) {
     for(int i=0; i<4; i++){
       if ((reg >> 4+i) & 1){
         note_midi(group,i+4,up);
       }
     }
   }
   else if (reg & 0x0F) { 
    for(int i=0; i<4; i++){
       if ((reg >> i) & 1){
         note_midi(group,i,up);
       }
     }     
   }
}

//The right two most bits turn on because those pins don't exist on the Uno
const char right_notes_midi_numbers[][8] = {
  {60,59,58,57,56,55},//54,53},
  {68,67,66,65,64,63},//62,61},
  {76,75,74,73,72,71,70,69},
  {84,83,82,81,80,79,78,77},
  {92,91,90,89,88,87,86,85},
  {0,0,0,0,0,0,0,93}
};

byte midi_channel1 = 0;
byte midi_channel2 = 1;
char notes_to_play;

void note_midi(int group, int position, boolean on){
  int pitch;
  String str_warn;
  char midi_cmd;
  char curr_register = 0;
  int midi_vel;

  pitch = right_notes_midi_numbers[group][position];
  curr_register = 0;

  if(on) {
    str_warn = "Note on ";
    midi_cmd = midi_channel2 | 0x90;
    KeysStatus[group] |= (1 << position);  //setting bit value
    Serial.print(" Changed Status: ");
    Serial.println(KeysStatus[group], BIN);
    midi_vel = 127;
  }
  else if(~on) {
    str_warn = "Note off ";
    midi_cmd = midi_channel2 | 0x80;
    KeysStatus[group] &= ~(1 << position);  //setting bit value
    Serial.print(" Changed Status: ");
    Serial.println(KeysStatus[group], BIN);
    midi_vel = 0;
  }
    
  Serial.print(str_warn);
  Serial.print(pitch,DEC);
  Serial.print(" Vel: ");
  Serial.println(midi_vel);
  Serial.print(" Group: ");
  Serial.println(group);
  Serial.print(" Position: ");
  Serial.println(position);
  
  notes_to_play = right_notes_midi_numbers[group][position];
  if (notes_to_play){
    //TODO - replace with ArduinoMIDI library command
    //Serial1.print(midi_cmd, BYTE);
    //Serial1.print(notes_to_play, BYTE);
    //Serial1.print(midi_vel, BYTE);
    Serial.print(" ");
    Serial.println(notes_to_play,DEC);
  }

}

// code stored in the sketch: Interruptor_Tutorial_1.ino
/* Analog Read Interrupter
* -----------------------
*/

int ruptPin = 2; // select the input pin for the interrupter
//int ruptPin = 16; // same as A2
int val = -1; // variable to store the value coming from the sensor

void setup()
{
    Serial.begin(9600); // set up Serial library at 9600 bps
    //pinMode(ruptPin,INPUT_PULLUP);
}

void loop()
{
    val = analogRead(ruptPin); // read the value from the sensor
    Serial.println(val); // print the sensor value to the serial monitor
    delay(500);
}

// code stored in the sketch: Interruptor_Tutorial_2.ino
/* 
* 2x2 matrix of Interruptors
* At this point most of this code is pulled directly from AccordionMega's code.
*/

int ANALOG_ROW1 = 2;//00000100
int ANALOG_ROW2 = 3;
char DIGITAL_COLUMNS[] = { 9, 10 };

int analog_val_1 = -1;
int analog_val_2 = -1;

//Note: in this example we're only using two bits from each byte
int KeysStatus[] = {  
  B0000000,
  B0000000
};

//this is the value of all pins from the analog port (7 and 6 don't exist on UNO)
//B00000000
//B76543210
byte reg_values = 0;

void setup()
{
    Serial.begin(9600);
    //Digital pins start turned off
    for (int i=0; i<sizeof(DIGITAL_COLUMNS);i++){ 
        pinMode(DIGITAL_COLUMNS[i],OUTPUT);
        digitalWrite(DIGITAL_COLUMNS[i], LOW);
    }

    //PortC as input 
    DDRC = B00000000;
    //Turn on pullup resistors
    PORTC = B11111111;
}

void loop()
{
  for (int i=0; i<sizeof(DIGITAL_COLUMNS);i++){ 
    //I wonder if we can replace this with direct port write for speed?
    digitalWrite(DIGITAL_COLUMNS[i], HIGH);
    delayMicroseconds(500);//TODO - play around with this number a bit

    delay(500);
    
    //PINB = 8-13 (14/15 don't work), PINC = analog 0-5 (6/7 don't work), PIND = 0-7
    reg_values = ~PINC;
    Serial.println(" ");
    Serial.print(" Previous Values for group ");
    Serial.print(i);
    Serial.print(": ");
    Serial.println(KeysStatus[i], BIN);
    Serial.print(" Values Read: ");
    Serial.println(reg_values, BIN);
    
    
    digitalWrite(DIGITAL_COLUMNS[i], LOW);

    if (reg_values != KeysStatus[i]){
      if (reg_values > KeysStatus[i]){             
        check_key(reg_values ^ KeysStatus[i],i,true);  //sending modified bits only
      }
      else {
        check_key(reg_values ^ KeysStatus[i],i,false); //sending modified bits only
      }           
    }
  }
}

void check_key(int reg, int group, boolean up){
   // saving 4 iterations, dividing byte by 2
   if (reg & 0xF0) {
     for(int i=0; i<4; i++){
       if ((reg >> 4+i) & 1){
         note_midi(group,i+4,up);
       }
     }
   }
   else if (reg & 0x0F) { 
    for(int i=0; i<4; i++){
       if ((reg >> i) & 1){
         note_midi(group,i,up);
       }
     }     
   }
}

const char right_notes_midi_numbers[][8] = {
  {60,59,58,57,56,55,54,53},
  {68,67,66,65,64,63,62,61},
  {76,75,74,73,72,71,70,69},
  {84,83,82,81,80,79,78,77},
  {92,91,90,89,88,87,86,85},
  {0,0,0,0,0,0,0,93}
};

byte midi_channel1 = 0;
byte midi_channel2 = 1;
char notes_to_play;

void note_midi(int group, int position, boolean on){
  int pitch;
  String str_warn;
  char midi_cmd;
  char curr_register = 0;
  int midi_vel;

  pitch = right_notes_midi_numbers[group][position];
  curr_register = 0;

  if(on) {
    str_warn = "Note on ";
    midi_cmd = midi_channel2 | 0x90;
    KeysStatus[group] |= (1 << position);  //setting bit value
    Serial.print(" Changed Status: ");
    Serial.println(KeysStatus[group], BIN);
    midi_vel = 127;
  }
  else if(~on) {
    str_warn = "Note off ";
    midi_cmd = midi_channel2 | 0x80;
    KeysStatus[group] &= ~(1 << position);  //setting bit value
    Serial.print(" Changed Status: ");
    Serial.println(KeysStatus[group], BIN);
    midi_vel = 0;
  }
    
  Serial.print(str_warn);
  Serial.print(pitch,DEC);
  Serial.print(" Vel: ");
  Serial.println(midi_vel);
  Serial.print(" Group: ");
  Serial.println(group);
  Serial.print(" Position: ");
  Serial.println(position);
  
  notes_to_play = right_notes_midi_numbers[group][position];
  if (notes_to_play){
    //TODO - replace with ArduinoMIDI library command
    //Serial1.print(midi_cmd, BYTE);
    //Serial1.print(notes_to_play, BYTE);
    //Serial1.print(midi_vel, BYTE);
    Serial.print(" ");
    Serial.println(notes_to_play,DEC);
  }

}

// code stored in the sketch: MIDI Tutorial.ino
/*
 MIDI note player

 This sketch shows how to use the serial transmit pin (pin 1) to send MIDI note data.
 If this circuit is connected to a MIDI synth, it will play
 the notes F#-0 (0x1E) to F#-5 (0x5A) in sequence.


 The circuit:
 * digital in 1 connected to MIDI jack pin 5
 * MIDI jack pin 2 connected to ground
 * MIDI jack pin 4 connected to +5V through 220-ohm resistor
 Attach a MIDI cable to the jack, then to a MIDI synth, and play music.

 created 13 Jun 2006
 modified 13 Aug 2012
 by Tom Igoe

 This example code is in the public domain.

 http://www.arduino.cc/en/Tutorial/Midi

 */

void setup() {
  //  Set MIDI baud rate:
  Serial.begin(31250);
}

void loop() {
  // play notes from F#-0 (0x1E) to F#-5 (0x5A):
  for (int note = 0x1E; note < 0x5A; note ++) {
    //Note on channel 1 (0x90), some note value (note), middle velocity (0x45):
    noteOn(0x90, note, 0x45);
    delay(100);
    //Note on channel 1 (0x90), some note value (note), silent velocity (0x00):
    noteOn(0x90, note, 0x00);
    delay(100);
  }
}

//  plays a MIDI note.  Doesn't check to see that
//  cmd is greater than 127, or that data values are  less than 127:
void noteOn(int cmd, int pitch, int velocity) {
  Serial.write(cmd);
  Serial.write(pitch);
  Serial.write(velocity);
}

// code stored in the sketch: MIDI_Accordion.ino
/* 
* MIDI Accordion
* Author: Brendan Vavra 
* Thanks to Dimon Yegorenkov for the original code of which much of this project is based.
*/
#include <MIDI.h>
#include <midi_Defs.h>
#include <midi_Message.h>
#include <midi_Namespace.h>
#include <midi_Settings.h>
struct MySettings : public midi::DefaultSettings
{
  //By default, the Arduino MIDI Library tries to be smart by 
  //excluding the CC byte if it doesn't change (to save bandwidth).
  //This is a problem when starting up Serial<->MIDI software
  //after starting up the Arduino because we miss the first CC byte.
  //Setting UseRunningStatus to false removes this "feature."
  //See https://github.com/projectgus/hairless-midiserial/issues/16 for details.
  static const bool UseRunningStatus = false;
  // Set MIDI baud rate. MIDI has a default baud rate of 31250,
  // but we're setting our baud rate higher so that the Serial<->MIDI software 
  // can properly decode and read outgoing MIDI data on the computer.
  static const long BaudRate = 115200;
};

//#define DEBUG//uncomment this line to print serial messages, comment to send MIDI data
//#define BLUETOOTH//uncomment this line to send MIDI data via bluetooth instead of USB
//#define BMP//uncomment this line to use the BMP180 to add dynamics via bellows

#ifdef BLUETOOTH
  MIDI_CREATE_CUSTOM_INSTANCE(HardwareSerial, Serial1, MIDI, MySettings);
#else
  MIDI_CREATE_CUSTOM_INSTANCE(HardwareSerial, Serial, MIDI, MySettings);
#endif

char left_hand_pins[] = { 10, 11, 12 };
// array to store up/down status of left keys
int LeftKeysStatus[] = {  
  B0000000,
  B0000000,
  B0000000
};
//Note: Based on how the opto-interruptors are laid out,
//You will likely have to remap their pitch numbers (36-59)
//36-47 are the bass notes, 48-59 are the chord notes
const char left_notes_midi_numbers[][8] = {
  {38,39,40,41,50,51,52,53},//10
  {46,47,36,37,58,59,48,49},//11
  {42,43,44,45,54,55,56,57} //12
};

char right_hand_pins[] = { 2, 3, 4, 5, 6, 7 };
// array to store up/down status of right keys
int RightKeysStatus[] = {  
  B0000000,
  B0000000,
  B0000000,
  B0000000,
  B0000000,
  B0000000
};
//Note: Based on how the opto-interruptors are laid out,
//You will likely have to remap their pitch numbers (53-93)
const char right_notes_midi_numbers[][8] = {
  {65,64,62,60,59,57,55,53},//2
  {79,77,76,74,72,71,69,67},//3
  {70,68,66,63,61,58,56,54},//4
  {93,91,89,88,86,84,83,81},//5
  {90,87,85,82,80,78,75,73},//6
  {92,0,0,0,0,0,0,0}        //7
};

void setup()
{
  #ifdef DEBUG
    Serial.begin(9600);
  #else
    MIDI.begin();
    //If we're sending MIDI over Serial1, open Serial for additional debugging
    #ifdef BLUETOOTH
      Serial.begin(9600);
    #endif
  #endif
  //Digital pins start turned off
  for (int i=0; i<sizeof(left_hand_pins);i++){ 
    pinMode(left_hand_pins[i],OUTPUT);
    digitalWrite(left_hand_pins[i], LOW);
  }
  for (int i=0; i<sizeof(right_hand_pins);i++){ 
    pinMode(right_hand_pins[i],OUTPUT);
    digitalWrite(right_hand_pins[i], LOW);
  }

  DDRF = B00000000;  // PortF as input (for left hand)
  PORTF = B11111111; // turn on pullup resistors

  DDRK = B00000000;  // PortK as input (for right hand)
  PORTK = B11111111; // turn on pullup resistors

  #ifdef BMP
    init_BMP();
  #endif
}

//MIDI Control Change code for expression, which is a percentage of velocity
const int CC_Expression = 11;
int prev_expression = 127;
//The BMP_180 is very sensitive, so readings can vary wildly from sample to sample.
//We're getting around this by computing and sending the average of bmp_sample_rate samples.
//A smaller bmp_sample_rate is more granular, but allows more "noise" to come in.
//A larger bmp_sample_rate is less granular, but has a smoother contour.
//Setting bmp_sample_rate too large may also lose the amount of perceived expression
//and create a noticable delay between squeezing the bellows and hearing the volume change,
//resulting in choppy crescendos and decrescendos.
//Tweak this value as needed.
const int bmp_sample_rate = 5;
int expression_avg[bmp_sample_rate];
int e = 0;

void loop()
{
  #ifdef BMP
    //Read pressure from the BMP_180 and convert it to MIDI expression
    int expression = get_expression(prev_expression);
    
    //Ignore it if it didn't change
    if(expression != prev_expression) {
      expression_avg[e] = expression;
      //Only send MIDI CC every bmp_sample_rate times, 
      //but send the average of the last bmp_sample_rate deltas
      if (e == bmp_sample_rate - 1){
        expression = 0;
        for (int i=0; i<bmp_sample_rate; i++){
          expression += expression_avg[i];
        }
        expression = expression/bmp_sample_rate;
        
        #ifdef DEBUG
          Serial.print("Expression Change: ");
          Serial.println(expression);
        #else
          MIDI.sendControlChange(CC_Expression,expression,1);
          //Don't let bass overpower melody
          MIDI.sendControlChange(CC_Expression,constrain(expression-6,0,127),2);
          //Don't let chords overpower melody
          MIDI.sendControlChange(CC_Expression,constrain(expression-12,0,127),3);
        #endif
        prev_expression = expression;
        e = 0;
      }
      else {
        e = e + 1;
      }
    }
  #endif

  //Alternate between scanning the left and right hand pins 
  //to reduce necessary delay between reads
  for (int i=0; i<6;i++){ 
    scan_pin(right_hand_pins[i], i, RightKeysStatus[i], false);
    scan_pin(left_hand_pins[i%3], i%3, LeftKeysStatus[i%3], true);
  }
  //Original
  //scan_keys(left_hand_pins, sizeof(left_hand_pins), LeftKeysStatus, true);
  //scan_keys(right_hand_pins, sizeof(right_hand_pins), RightKeysStatus, false);
}

//This function is currently unused
void scan_keys(char *pins, int pinLength, int *KeysStatus, bool left) {
  for (int i=0; i<pinLength;i++){ 
    scan_pin(pins[i], i, KeysStatus[i], left);
  }
}

byte reg_values = 0;

//Read the analog port value for the given pin
//If something changed, trigger MIDI signal
void scan_pin(int pin, int index, byte PinStatus, bool left) {
  //TODO - I wonder if we can replace this with direct port write for even better performance?
  digitalWrite(pin, HIGH);
  //A slight delay is needed here or else we'll be reading the previous pin
  delayMicroseconds(300);//was able to cut this in half by alternating between left and right
  if (left) {
    reg_values = ~PINF;
  }
  else {
    reg_values = ~PINK;
  }
  digitalWrite(pin, LOW);

  //check if something changed
  if (reg_values != PinStatus){ 
    //if the byte value is greater, we're turning the note on; else, turning it off.
    if (reg_values > PinStatus){
      //using bit-wise OR to send modified bits only
      check_key(reg_values ^ PinStatus, index, true, left); 
    }
    else {
      check_key(reg_values ^ PinStatus, index, false, left);
    }
  }
}

//Check to see which bits have changed and send the appropriate midi message
//Instead of iterating the array from 0-7, use binary search to find the modified bits faster
void check_key(int reg, int group, boolean on, boolean left){
  // saving 4 iterations, dividing byte by 2
  if (reg & 0xF0) {
    for(int i=0; i<4; i++){
      if ((reg >> 4+i) & 1){
        note_midi(group, i+4, on, left);
      }
    }
  }
  else if (reg & 0x0F) { 
    for(int i=0; i<4; i++){
      if ((reg >> i) & 1){
        note_midi(group, i, on, left);
      }
    }
  }
}

void note_midi(int group, int position, boolean on, boolean left){
  int pitch;
  int channel = 1;
  int midi_vel = 127;

  if (left){
    if (on){
      LeftKeysStatus[group] |= (1 << position);  //setting bit value
    }
    else {
      LeftKeysStatus[group] &= ~(1 << position);  //setting bit value
    }
    pitch = left_notes_midi_numbers[group][position];
    if(pitch < 48) {
      midi_vel = 120;//Don't let bass overpower melody
      channel = 2;
    }
    else {
      midi_vel = 110;//Don't let chords overpower melody
      channel = 3;
    }
  }
  else{
    if(on) {
      RightKeysStatus[group] |= (1 << position);  //setting bit value
    }
    else {
      RightKeysStatus[group] &= ~(1 << position);  //setting bit value
    }
    pitch = right_notes_midi_numbers[group][position];
    channel = 1;
  }

  if (pitch){
    #ifdef DEBUG
      Serial.print("Note ");
      if(on){
        Serial.print("on: ");
      }
      else {
        Serial.print("off: ");
      }
      Serial.println(pitch);
    #else
      if(on) {
        MIDI.sendNoteOn(pitch, midi_vel, channel);
      }
      else {
        MIDI.sendNoteOff(pitch, midi_vel, channel);
      }
    #endif
  }

}

// code stored in the sketch: MIDI_Tutorial_1.ino
#include <MIDI.h>
#include <midi_Defs.h>
#include <midi_Message.h>
#include <midi_Namespace.h>
#include <midi_Settings.h>

/*
 MIDI note player

 This sketch shows how to use the serial transmit pin (pin 1) to send MIDI note data.
 If this circuit is connected to a MIDI synth, it will play
 the notes F#-0 (0x1E) to F#-5 (0x5A) in sequence.

 The circuit:
 * digital in 1 connected to MIDI jack pin 5
 * MIDI jack pin 2 connected to ground
 * MIDI jack pin 4 connected to +5V through 220-ohm resistor
 Attach a MIDI cable to the jack, then to a MIDI synth, and play music.

 This example code is in the public domain.
 http://www.arduino.cc/en/Tutorial/Midi

 */


MIDI_CREATE_DEFAULT_INSTANCE();

void setup() {
  MIDI.begin(1);
  //  Set MIDI baud rate:
  Serial.begin(115200);
}

void loop() {
  // play notes from F#-0 (0x1E) to F#-5 (0x5A):
  for (int note = 0x1E; note < 0x5A; note ++) {

    MIDI.sendNoteOn(note,127,1);  // Send a Note (pitch note, velo 127 on channel 1)
    delay(1000);                // Wait for a second
    MIDI.sendNoteOff(note,127,1);
    
  }
}
