# Fritzing sketch BMP_Tutorial (saved by Fritzing 0.9.3b)

parts:
  Arduino = Arduino Uno (Rev3)
  Part1 = Barometric Pressure Sensor - BMP085 Breakout

nets:
  N1: Arduino.A4/SDA, Part1.SDA
  N2: Arduino.A5/SCL, Part1.SCL
  GND: Arduino.GND, Part1.GND
  3V3: Arduino.3V3, Part1.VCC

notes:
  The part says BMP085, but the BMP180 is functionally equivalent
  SDA and SCL pins go to A4 and A5 respectively on the Uno. On the Mega they go to reserved pins 20 and 21.

// code stored in the sketch: BMP_Tutorial.ino
/*
  Barometric Pressure Sensor
  Author: Brendan Vavra

  This sketch shows how to use the BMP180 to read changes in air pressure
  and convert the values to MIDI velocity.

  Based off SparkFun's BMP library examples

  Circuit:
  - BMP180 Vcc to Arduino 3.3V
  - BMP180 GND to Arduino GND
  - BMP180 SDA to Arduino SDA (A4 for Uno, 20 for Mega)
  - BMP180 SCL to Arduino SCL (A5 for Uno, 21 for Mega)

  From the doc page: 
  https://learn.sparkfun.com/tutorials/bmp180-barometric-pressure-sensor-hookup-
  "Note that it is safe to connect the SCA and SDL pins to an 
  I2C port on a 5V Arduino, as the pullup resistors on the 
  BMP180 board will keep the voltage below 3.6V."

  Blowing lightly on the sensor should change the pressure reading
  and, hence, the velocity.
*/
#include <SFE_BMP180.h>
#include <Wire.h>

SFE_BMP180 pressure;

char status;
double Temp, Calib_Pressure, Pressure;
int Pressure_Delta;

void setup() {
  Serial.begin(9600);

  Serial.println("REBOOT");
  // Initialize the sensor 
  //(it is important to get calibration values stored on the device).
  if (pressure.begin())
  {
    Serial.println("BMP180 init success");

    status = pressure.startTemperature();
    if (status != 0)
    {
      // Wait for the measurement to complete:
      delay(status);
  
      // Retrieve the completed temperature measurement:
      // Function returns 1 if successful, 0 if failure.
      status = pressure.getTemperature(Temp);//sets temperature
      if (status != 0)
      {
        // Print out the measurement:
        Serial.print("temperature: ");
        Serial.print((9.0/5.0)*Temp+32.0,2);//Temp is in C - converting to F
        Serial.println(" deg F");
        for (int i=0; i<32; i++){
          Calib_Pressure += readPressure();
        }
        Calib_Pressure = Calib_Pressure/32;
      }
      else Serial.println("error retrieving temperature measurement\n");
    }
    else Serial.println("error starting temperature measurement\n");
  }
  else
  {
    // Oops, something went wrong, this is usually a connection problem,
    Serial.println("BMP180 init fail\n\n");
    while(1); // Pause forever.
  }
}

void loop() {
  Serial.println("=====================");
  Pressure = readPressure();
  Serial.print("Calib_Pressure: ");
  Serial.println(Calib_Pressure);
  Pressure_Delta = abs(Pressure - Calib_Pressure);
  Serial.print("Velocity delta: ");
  Serial.println(Pressure_Delta);
  Pressure_Delta = constrain(Pressure_Delta, 10, 127);
  Serial.print("Velocity value: ");
  Serial.println(Pressure_Delta);
  delay(1000);
}

double readPressure() {
  // Start a pressure measurement:
  // The parameter is the oversampling setting, 
  // from 0 to 3 (highest res, longest wait).
  // If request is successful, the number of ms to wait is returned.
  // If request is unsuccessful, 0 is returned.
  double P, p0;
  status = pressure.startPressure(3);//We probably want 0, for speed
  if (status != 0)
  {
    // Wait for the measurement to complete:
    delay(status);

    // Retrieve the completed pressure measurement using the given temp:
    // (If temperature is stable, you can do one temperature measurement 
    // for a number of pressure measurements.)
    // Function returns 1 if successful, 0 if failure.
    status = pressure.getPressure(P,Temp);//sets P to pressure
    if (status != 0)
    {
      // Print out the measurement:
      Serial.print("Pressure: ");
      Serial.print(P,2);
      Serial.print(" mb, ");
      Serial.print(P*0.0295333727,2);
      Serial.println(" inHg");
    }
    else {
      Serial.println("error retrieving pressure measurement\n");
    }
  }
  else {
    Serial.println("error starting pressure measurement\n");
  }
  return P*100;//P is in millibars, but AccordionMega's code expects pascals
}

// code stored in the sketch: MIDI Tutorial.ino
/*
 MIDI note player

 This sketch shows how to use the serial transmit pin (pin 1) to send MIDI note data.
 If this circuit is connected to a MIDI synth, it will play
 the notes F#-0 (0x1E) to F#-5 (0x5A) in sequence.


 The circuit:
 * digital in 1 connected to MIDI jack pin 5
 * MIDI jack pin 2 connected to ground
 * MIDI jack pin 4 connected to +5V through 220-ohm resistor
 Attach a MIDI cable to the jack, then to a MIDI synth, and play music.

 created 13 Jun 2006
 modified 13 Aug 2012
 by Tom Igoe

 This example code is in the public domain.

 http://www.arduino.cc/en/Tutorial/Midi

 */

void setup() {
  //  Set MIDI baud rate:
  Serial.begin(31250);
}

void loop() {
  // play notes from F#-0 (0x1E) to F#-5 (0x5A):
  for (int note = 0x1E; note < 0x5A; note ++) {
    //Note on channel 1 (0x90), some note value (note), middle velocity (0x45):
    noteOn(0x90, note, 0x45);
    delay(100);
    //Note on channel 1 (0x90), some note value (note), silent velocity (0x00):
    noteOn(0x90, note, 0x00);
    delay(100);
  }
}

//  plays a MIDI note.  Doesn't check to see that
//  cmd is greater than 127, or that data values are  less than 127:
void noteOn(int cmd, int pitch, int velocity) {
  Serial.write(cmd);
  Serial.write(pitch);
  Serial.write(velocity);
}

// code stored in the sketch: MIDI_Tutorial.ino
/*
  MIDI note player
  Author: Brendan Vavra

  This sketch shows how to use the serial transmit pin (pin 1) to send MIDI note data.
  If this circuit is connected to a MIDI synth, it will play
  the notes from F3 (53) to A6 (93) in sequence.

  This tutorial has been modified to use the Arduino MIDI library:
  http://playground.arduino.cc/Main/MIDILibrary
  Original code is in the public domain:
  http://www.arduino.cc/en/Tutorial/Midi

  If using a serial-to-MIDI converter, no circuit components are necessary.
  If sending MIDI over a MIDI cable, the circuit is as follows:
  - digital in 1 connected to MIDI jack pin 5
  - MIDI jack pin 2 connected to ground
  - MIDI jack pin 4 connected to +5V through 220-ohm resistor
  Attach a MIDI cable to the jack, then to a MIDI synth (or PC), and play music.
*/
#include <MIDI.h>
#include <midi_Defs.h>
#include <midi_Message.h>
#include <midi_Namespace.h>
#include <midi_Settings.h>

MIDI_CREATE_DEFAULT_INSTANCE();

void setup() {
  MIDI.begin(1);
  // Set MIDI baud rate. MIDI has a single baud rate of 31250,
  // but we're setting the serial baud rate higher to help reduce latency.
  Serial.begin(115200);
}

void loop() {
  int velocity = 127; //Max Velocity (range is 0-127)
  int channel = 1; //MIDI Channel 1 (out of 16)
  // Play notes from F3 (53) to A6 (93):
  for (int note = 53; note <= 93; note ++) {
    // Send a NoteOn message, wait a second, turn the note off
    MIDI.sendNoteOn(note, velocity, channel);  
    delay(1000);
    MIDI.sendNoteOff(note, velocity, channel);
  }
}

// code stored in the sketch: MIDI_Tutorial_1.ino
#include <MIDI.h>
#include <midi_Defs.h>
#include <midi_Message.h>
#include <midi_Namespace.h>
#include <midi_Settings.h>

/*
 MIDI note player

 This sketch shows how to use the serial transmit pin (pin 1) to send MIDI note data.
 If this circuit is connected to a MIDI synth, it will play
 the notes F#-0 (0x1E) to F#-5 (0x5A) in sequence.


 The circuit:
 * digital in 1 connected to MIDI jack pin 5
 * MIDI jack pin 2 connected to ground
 * MIDI jack pin 4 connected to +5V through 220-ohm resistor
 Attach a MIDI cable to the jack, then to a MIDI synth, and play music.

 created 13 Jun 2006
 modified 13 Aug 2012
 by Tom Igoe

 This example code is in the public domain.

 http://www.arduino.cc/en/Tutorial/Midi

 */


MIDI_CREATE_DEFAULT_INSTANCE();

void setup() {
  MIDI.begin(1);
  //  Set MIDI baud rate:
  Serial.begin(115200);
}

void loop() {
  // play notes from F#-0 (0x1E) to F#-5 (0x5A):
  for (int note = 0x1E; note < 0x5A; note ++) {

    MIDI.sendNoteOn(note,127,1);  // Send a Note (pitch note, velo 127 on channel 1)
    delay(1000);                // Wait for a second
    MIDI.sendNoteOff(note,127,1);
    
  }
}
