# Fritzing sketch Bluetooth_Tutorial_2 (saved by Fritzing 0.9.3b)
breadboards: 1

parts:
  R1 = Resistor [tolerance=±5% resistance=1k package="0603 [SMD]"]
  R2 = Resistor [tolerance=±5% resistance=2.2k package="0603 [SMD]"]
  Arduino = Arduino Uno (Rev3)
  R3 = Resistor [tolerance=±5% resistance=1k package="0603 [SMD]"]
  R4 = Resistor [tolerance=±5% resistance=2.2k package="0603 [SMD]"]
  HC-05 = Bluetooth HC-05 Macho

nets:
  N1: R1.Pin_0, R2.Pin_1, HC-05.RXD
  N2: R1.Pin_1, Arduino.D11_PWM/MOSI
  GND: R2.Pin_0, Arduino.GND, R4.Pin_0, HC-05.GND
  N3: Arduino.D9_PWM, R3.Pin_1
  N4: Arduino.D10_PWM/SS, HC-05.TXD
  3V3: Arduino.3V3, HC-05.VCC
  N5: R3.Pin_0, R4.Pin_1, HC-05.Key

notes:
  Arduino Bluetooth AT Commands Tutorials
  http://www.instructables.com/id/Modify-The-HC-05-Bluetooth-Module-Defaults-Using-A/?ALLSTEPS
  http://www.martyncurrey.com/arduino-with-hc-05-bluetooth-module-at-mode/
  Voltage dividers required on pins 9 and 11 to convert 5V from Arduino to 3.3V going to HC-05
  Tutorial uses 1k and 2k - you can also use 10k and 20k (I used 3 10ks since that's all I had)
  If your HC-05 has a KEY/EN button on it, you don't need to wire it to the Arduino. Just hold the button when turning it on, and hold the button whenever you send a command. This wire is just the equivalent of holding the button for you.
  Disconnect the 3.3V wire before connecting the arduino to the USB

// code stored in the sketch: Bluetooth_Tutorial.ino
//////////////////////////////////////////////////////////////////////////////////
// REMIXED BY: TECHBITAR (HAZIM BITAR)
// LICENSE: PUBLIC DOMAIN
// DATE: MAY 2, 2012
// CONTACT: techbitar at gmail dot com

int counter =0;

void setup() {
  Serial.begin(9600); 
  delay(50);
}

void loop() {
  counter++;
  Serial.print("Arduino counter: ");
  Serial.println(counter);
  delay(500); // wait half a sec
}

// code stored in the sketch: Bluetooth_Tutorial_2.ino
/*
  Bluetooth HC-05 AT Command Mode
  Author: Brendan Vavra

  This is a program to set AT commands on the HC-05 Bluetooth transceiver.
  Made with the help of these links:
  http://www.instructables.com/id/Modify-The-HC-05-Bluetooth-Module-Defaults-Using-A/?ALLSTEPS
  http://www.martyncurrey.com/arduino-with-hc-05-bluetooth-module-at-mode/

  Circuit:
  - Bluetooth TX to Arduino PIN 10
  - Bluetooth RX to Arduino PIN 11 (via voltage divider)
  - Bluetooth GND to Arduino GND
  - Bluetooth Vcc to Arduino 3.3V
  - Bluetooth KEY to Arduino PIN 9 (via voltage divider)

  HC-05 AT COMMANDS
  AT : Ceck the connection.
  AT+NAME : See default name
  AT+ADDR : See default address
  AT+VERSION : See version
  AT+UART : See baudrate
  AT+ROLE: See role of bt module(1=master/0=slave)
  AT+RESET : Reset and exit AT mode
  AT+ORGL : Restore factory settings
  AT+PSWD: See default password

  To change device name from the default HC-05 to let's say MYBLUE enter: "AT+NAME=MYBLUE"
  To change default security code from 1234 to 2987 enter: "AT+PSWD=2987"
  To change HC-05 baud rate from default 9600 to 115200, 1 stop bit, 0 parity enter: "AT+UART=115200,1,0"

  Required for MIDI Accordion:
  - Setting baud rate to 115200
    AT+UART=115200,1,0
  Optional:
  - Setting device name (this is displayed under list of connected Bluetooth devices)
    AT+NAME=MIDI ACCORDION
  - Setting password
*/

#include <SoftwareSerial.h>

SoftwareSerial BTSerial(10, 11); // Setting soft RX | TX pins

void setup()
{
  Serial.begin(9600);
  // This pin will pull the HC-05 pin 34 (KEY pin) HIGH to switch module to AT mode
  pinMode(9, OUTPUT);  
  digitalWrite(9, HIGH);
  Serial.println("Enter AT commands:");
  BTSerial.begin(38400);  // HC-05 baud rate in AT command mode
}

void loop()
{
  // Keep reading from HC-05 and send to Arduino Serial Monitor
  if (BTSerial.available())
  {
    Serial.write(BTSerial.read());
  }

  // Keep reading from Arduino Serial Monitor and send to HC-05
  if (Serial.available())
  {
    BTSerial.write(Serial.read());
  }
}
