# Fritzing sketch Bluetooth_Tutorial (saved by Fritzing 0.9.2b)
breadboards: 1

parts:
  R1 = Resistor [tolerance=±5% resistance=10k package="0603 [SMD]"]
  R2 = Resistor [tolerance=±5% resistance=22k package="0603 [SMD]"]
  HC-05 = HC-05 [package=1x06-smd-female-v2]
  Arduino = Arduino Uno (Rev3)

nets:
  N1: R1.Pin_0, R2.Pin_1, HC-05.RXD
  N2: R1.Pin_1, Arduino.D1/TX
  GND: R2.Pin_0, HC-05.GND, Arduino.GND
  N3: HC-05.TXD, Arduino.D0/RX
  VCC: HC-05.VCC, Arduino.3V3

notes:
  Arduino Bluetooth Tutorial
  http://www.instructables.com/id/Cheap-2-Way-Bluetooth-Connection-Between-Arduino-a/?ALLSTEPS
  TODO - replace Header 6 icon with Bluetooth HC-05 icon
  Connect power to battery to eliminate wired Serial connection
  Voltage divider required to convert 5V from Arduino to 3.3V going to HC-05
  Tutorial uses 1k and 2k - I used 3 10ks (since that's all I had)

custom parts:
  HC-05: HC-05 Bluetooth Transceiver with 6-pin 0.1 header.

// code stored in the sketch: Bluetooth_Tutorial.ino
/*
  Bluetooth Serial Output
  Author: Brendan Vavra

  This is a simple counter to test sending data over a wireless Bluetooth connection.

  Circuit:
  - Bluetooth TX to Arduino RX
  - Bluetooth RX to Arduino TX (with voltage divider)
  - Bluetooth GND to Arduino GND
  - Bluetooth Vcc to Arduino 3.3V

  If everything is connected properly, you should be able to see the serial output
  using a terminal emulator such as TeraTerm: https://en.osdn.jp/projects/ttssh2/releases/
  
  Detailed instructions for connecting an HC-05 Bluetooth transceiver can be found here:
  http://www.instructables.com/id/Cheap-2-Way-Bluetooth-Connection-Between-Arduino-a/
*/
int counter = 0;

void setup() {
  Serial.begin(9600);
}

void loop() {
  counter++;
  Serial.print("Arduino counter: ");
  Serial.println(counter);
  delay(500);
}
