# Fritzing sketch Bluetooth_Tutorial_2 (saved by Fritzing 0.9.2b)
breadboards: 1

parts:
  R1 = Resistor [tolerance=±5% resistance=10k package="0603 [SMD]"]
  R2 = Resistor [tolerance=±5% resistance=22k package="0603 [SMD]"]
  HC-05 = HC-05 [package=1x06-smd-female-v2]
  Arduino = Arduino Uno (Rev3)
  R3 = Resistor [tolerance=±5% resistance=1k package="0603 [SMD]"]
  R4 = Resistor [tolerance=±5% resistance=22k package="0603 [SMD]"]

nets:
  N1: R1.Pin_0, R2.Pin_1, HC-05.RXD
  N2: R1.Pin_1, Arduino.D11_PWM/MOSI
  GND: R2.Pin_0, HC-05.GND, Arduino.GND, R4.Pin_0
  N3: HC-05.TXD, Arduino.D10_PWM/SS
  VCC: HC-05.VCC, Arduino.3V3
  N4: HC-05.EN, R3.Pin_0, R4.Pin_1
  N5: Arduino.D9_PWM, R3.Pin_1

notes:
  Arduino Bluetooth AT Commands Tutorials
  http://www.instructables.com/id/Modify-The-HC-05-Bluetooth-Module-Defaults-Using-A/?ALLSTEPS
  http://www.martyncurrey.com/arduino-with-hc-05-bluetooth-module-at-mode/
  TODO - replace Header 6 icon with Bluetooth HC-05 icon
  Voltage dividers required on pins 9 and 11 to convert 5V from Arduino to 3.3V going to HC-05
  Tutorial uses 1k and 2k - I used 3 10ks (since that's all I had)
  If your HC-05 has a KEY/EN button on it, you don't need to wire it to the Arduino. Just hold the button when turning it on, and hold the button whenever you send a command. This wire is just the equivalent of holding the button for you.
  Disconnect the 3.3V wire before connecting the arduino to the USB

custom parts:
  HC-05: HC-05 Bluetooth Transceiver with 6-pin 0.1 header.

// code stored in the sketch: Bluetooth_Tutorial.ino
//////////////////////////////////////////////////////////////////////////////////
// REMIXED BY: TECHBITAR (HAZIM BITAR)
// LICENSE: PUBLIC DOMAIN
// DATE: MAY 2, 2012
// CONTACT: techbitar at gmail dot com

int counter =0;

void setup() {
  Serial.begin(9600); 
  delay(50);
}

void loop() {
  counter++;
  Serial.print("Arduino counter: ");
  Serial.println(counter);
  delay(500); // wait half a sec
}

// code stored in the sketch: Bluetooth_Tutorial_2.ino

/* AT COMMANDS
 * AT : Ceck the connection.
 * AT+NAME : See default name
 * AT+ADDR : see default address
 * AT+VERSION : See version
 * AT+UART : See baudrate
 * AT+ROLE: See role of bt module(1=master/0=slave)
 * AT+RESET : Reset and exit AT mode
 * AT+ORGL : Restore factory settings
 * AT+PSWD: see default password
 * 
 * Changing values:
 * AT+NAME=MIDI ACCORDION
 * AT+UART=115200,1,0
 * 
 * To change device name from the default HC-05 to let's say MYBLUE enter: "AT+NAME=MYBLUE"
 * To change default security code from 1234 to 2987 enter: "AT+PSWD=2987"
 * To change HC-05 baud rate from default 9600 to 115200, 1 stop bit, 0 parity enter: "AT+UART=115200,1,0"
 */

#include <SoftwareSerial.h>

SoftwareSerial BTSerial(10, 11); // RX | TX

void setup()
{
  Serial.begin(9600);
  pinMode(9, OUTPUT);  // this pin will pull the HC-05 pin 34 (key pin) HIGH to switch module to AT mode
  digitalWrite(9, HIGH);
  Serial.println("Enter AT commands:");
  BTSerial.begin(38400);  // HC-05 default speed in AT command more
}

void loop()
{

  // Keep reading from HC-05 and send to Arduino Serial Monitor
  if (BTSerial.available())
    Serial.write(BTSerial.read());

  // Keep reading from Arduino Serial Monitor and send to HC-05
  if (Serial.available())
    BTSerial.write(Serial.read());
}
