# Fritzing sketch MIDI_Tutorial (saved by Fritzing 0.9.2b)
breadboards: 1

parts:
  Arduino = Arduino Uno (Rev3)
  R1 = Resistor [tolerance=±5% resistance=220 package="0603 [SMD]"]
  R2 = Resistor [tolerance=±5% resistance=220 package="0603 [SMD]"]
  DIN1 = DIN-5 jack (MIDI) [package=THT]

nets:
  N1: Arduino.D1/TX, R1.Pin_0
  N2: Arduino.5V, R2.Pin_0
  N3: Arduino.GND, DIN1.2
  N4: R1.Pin_1, DIN1.5
  N5: R2.Pin_1, DIN1.4

notes:
  Arduino MIDI Tutorial
  http://www.arduino.cc/en/Tutorial/Midi
  Make sure PIN4 (right) goes to 5V and PIN5 (left) goes to Serial OUT (TX)
  MIDI Cable is connected with the IN port

// code stored in the sketch: MIDI Tutorial.ino
/*
 MIDI note player

 This sketch shows how to use the serial transmit pin (pin 1) to send MIDI note data.
 If this circuit is connected to a MIDI synth, it will play
 the notes F#-0 (0x1E) to F#-5 (0x5A) in sequence.


 The circuit:
 * digital in 1 connected to MIDI jack pin 5
 * MIDI jack pin 2 connected to ground
 * MIDI jack pin 4 connected to +5V through 220-ohm resistor
 Attach a MIDI cable to the jack, then to a MIDI synth, and play music.

 created 13 Jun 2006
 modified 13 Aug 2012
 by Tom Igoe

 This example code is in the public domain.

 http://www.arduino.cc/en/Tutorial/Midi

 */

void setup() {
  //  Set MIDI baud rate:
  Serial.begin(31250);
}

void loop() {
  // play notes from F#-0 (0x1E) to F#-5 (0x5A):
  for (int note = 0x1E; note < 0x5A; note ++) {
    //Note on channel 1 (0x90), some note value (note), middle velocity (0x45):
    noteOn(0x90, note, 0x45);
    delay(100);
    //Note on channel 1 (0x90), some note value (note), silent velocity (0x00):
    noteOn(0x90, note, 0x00);
    delay(100);
  }
}

//  plays a MIDI note.  Doesn't check to see that
//  cmd is greater than 127, or that data values are  less than 127:
void noteOn(int cmd, int pitch, int velocity) {
  Serial.write(cmd);
  Serial.write(pitch);
  Serial.write(velocity);
}

// code stored in the sketch: MIDI_Tutorial.ino
/*
  MIDI note player
  Author: Brendan Vavra

  This sketch shows how to use the serial transmit pin (pin 1) to send MIDI note data.
  If this circuit is connected to a MIDI synth, it will play
  the notes from F3 (53) to A6 (93) in sequence.

  This tutorial has been modified to use the Arduino MIDI library:
  http://playground.arduino.cc/Main/MIDILibrary
  Original code is in the public domain:
  http://www.arduino.cc/en/Tutorial/Midi

  If using a serial-to-MIDI converter, no circuit components are necessary.
  If sending MIDI over a MIDI cable, the circuit is as follows:
  - digital in 1 connected to MIDI jack pin 5
  - MIDI jack pin 2 connected to ground
  - MIDI jack pin 4 connected to +5V through 220-ohm resistor
  Attach a MIDI cable to the jack, then to a MIDI synth (or PC), and play music.
*/
#include <MIDI.h>
#include <midi_Defs.h>
#include <midi_Message.h>
#include <midi_Namespace.h>
#include <midi_Settings.h>

MIDI_CREATE_DEFAULT_INSTANCE();

void setup() {
  MIDI.begin(1);
  // Set MIDI baud rate. MIDI has a single baud rate of 31250,
  // but we're setting the serial baud rate higher to help reduce latency.
  Serial.begin(115200);
}

void loop() {
  int velocity = 127; //Max Velocity (range is 0-127)
  int channel = 1; //MIDI Channel 1 (out of 16)
  // Play notes from F3 (53) to A6 (93):
  for (int note = 53; note <= 93; note ++) {
    // Send a NoteOn message, wait a second, turn the note off
    MIDI.sendNoteOn(note, velocity, channel);  
    delay(1000);
    MIDI.sendNoteOff(note, velocity, channel);
  }
}

// code stored in the sketch: MIDI_Tutorial_1.ino
#include <MIDI.h>
#include <midi_Defs.h>
#include <midi_Message.h>
#include <midi_Namespace.h>
#include <midi_Settings.h>

/*
 MIDI note player

 This sketch shows how to use the serial transmit pin (pin 1) to send MIDI note data.
 If this circuit is connected to a MIDI synth, it will play
 the notes F#-0 (0x1E) to F#-5 (0x5A) in sequence.


 The circuit:
 * digital in 1 connected to MIDI jack pin 5
 * MIDI jack pin 2 connected to ground
 * MIDI jack pin 4 connected to +5V through 220-ohm resistor
 Attach a MIDI cable to the jack, then to a MIDI synth, and play music.

 created 13 Jun 2006
 modified 13 Aug 2012
 by Tom Igoe

 This example code is in the public domain.

 http://www.arduino.cc/en/Tutorial/Midi

 */


MIDI_CREATE_DEFAULT_INSTANCE();

void setup() {
  MIDI.begin(1);
  //  Set MIDI baud rate:
  Serial.begin(115200);
}

void loop() {
  // play notes from F#-0 (0x1E) to F#-5 (0x5A):
  for (int note = 0x1E; note < 0x5A; note ++) {

    MIDI.sendNoteOn(note,127,1);  // Send a Note (pitch note, velo 127 on channel 1)
    delay(1000);                // Wait for a second
    MIDI.sendNoteOff(note,127,1);
    
  }
}
