# Fritzing sketch Opto_Interruptor_1_rev (saved by Fritzing 0.9.2b)
breadboards: 1

parts:
  Arduino = Arduino Uno (Rev3)
  R1 = Resistor [tolerance=±5% resistance=220 package="0603 [SMD]"]
  Q1 = PHOTOTRANSISTOR REFLECTIVE OBJECT SENSOR [package=qrb1114-side]
  R3 = Resistor [tolerance=±5% resistance=1k package="0603 [SMD]"]
  Q2 = NPN-Transistor [package="TO92 [THT]"]

nets (from the schematic view):
  N1: Arduino.A2, Q1.C
  N2: Arduino.D9_PWM, R3.Pin_0
  N3: Arduino.GND, Q1.E, Q2.E
  N4: Arduino.5V, R1.Pin_0
  N5: R1.Pin_1, Q1.A
  N6: Q1.K, Q2.C
  N7: R3.Pin_1, Q2.B

notes:
  This is a modified version of the interruptor prototype. This more closely resembles the schematics AccordionMega wrote up (uses internal pullup resistor instead of external pulldown resistor).
  The resistor to use in front of the diode will depend on the type of interruptor. It'll probably be somewhere between 100 and 330Ω. I'm using 270Ω right now.
  //TODO: replace QRB1114 image with something that looks more like our interruptors (this one is a bit confusing)
  <- Diode
  <- Transistor

// code stored in the sketch: Interruptor_1_Uno.ino
/* Analog and Digital Read Interrupter
 *  Author: Brendan Vavra
 *  
 *  This is testing that the interruptor reads a signal from the diode
 *  and that the value changes if the diode is blocked OR 
 *  the digital pin connected to the diode is turned LOW/HIGH
 *  
 */
byte reg_values = 0;
int ruptPin = 2; // select the input pin for the interrupter
int val = -1; // variable to store the value coming from the sensor

void setup()
{
    Serial.begin(9600); // set up Serial library at 9600 bps
    pinMode(9,OUTPUT);
    digitalWrite(9, HIGH);

    DDRC = B00000000;// PortC as input (for Arduino Uno)
    PORTC = B11111111;// turn on pullup resistors
}

void loop()
{
    digitalWrite(9, HIGH);
    delay(1);
    val = analogRead(ruptPin); // read the value from the sensor
    reg_values = ~PINC;
    Serial.print("PIN HIGH: ");
    Serial.println(val); // print the sensor value to the serial monitor
    Serial.println(reg_values, BIN);
    Serial.println("");
    delay(2000);

    digitalWrite(9, LOW);
    delay(1);
    val = analogRead(ruptPin); // read the value from the sensor
    reg_values = ~PINC;
    Serial.print("PIN LOW: ");
    Serial.println(val); // print the sensor value to the serial monitor
    Serial.println(reg_values, BIN);
    Serial.println("");
    delay(2000);

    /*
     * Things to try:
     * - using internal pullup*
     * - changing external pullup
     * - reversing the digital pin (to match Accordion Mega)
     * - reading it digitally
     * - adding that second interruptor...
     */
}

// code stored in the sketch: Interruptor_Tutorial_1a.ino
/* Analog Read Interrupter
*/

int ruptPin = 2; //input pin for the interrupter
int val = -1; //analog value coming from the sensor
byte reg_values = 0;
int initial_us = 0;
int final_us = 0;

void setup()
{
    Serial.begin(9600); // set up Serial library at 9600 bps
    pinMode(9,OUTPUT);
    digitalWrite(9, HIGH);
    
    DDRC = B00000000;// PortC as input (for Arduino Uno)
    PORTC = B11111111;// turn on pullup resistors
}

void loop()
{
    //time how long it takes to do an analogRead
    initial_us = micros();
    val = analogRead(ruptPin); // read the value from the sensor
    final_us = micros();
    Serial.print("Value for analog PIN: ");
    Serial.println(val); // print the sensor value to the serial monitor
    Serial.print("Time for analogRead(): ");
    Serial.println(final_us-initial_us);//c. 115us per PIN

    //time how long it takes to read the entire port directly
    initial_us = micros();
    reg_values = ~PINC;
    final_us = micros();
    Serial.print("Value for analog PORT: ");
    Serial.println(reg_values, BIN);
    Serial.print("Time for portRead(): ");
    Serial.println(final_us-initial_us);//c. 4us for all 6 PINs
    Serial.println("");
    delay(1000);
}

// code stored in the sketch: MIDI Tutorial.ino
/*
 MIDI note player

 This sketch shows how to use the serial transmit pin (pin 1) to send MIDI note data.
 If this circuit is connected to a MIDI synth, it will play
 the notes F#-0 (0x1E) to F#-5 (0x5A) in sequence.


 The circuit:
 * digital in 1 connected to MIDI jack pin 5
 * MIDI jack pin 2 connected to ground
 * MIDI jack pin 4 connected to +5V through 220-ohm resistor
 Attach a MIDI cable to the jack, then to a MIDI synth, and play music.

 created 13 Jun 2006
 modified 13 Aug 2012
 by Tom Igoe

 This example code is in the public domain.

 http://www.arduino.cc/en/Tutorial/Midi

 */

void setup() {
  //  Set MIDI baud rate:
  Serial.begin(31250);
}

void loop() {
  // play notes from F#-0 (0x1E) to F#-5 (0x5A):
  for (int note = 0x1E; note < 0x5A; note ++) {
    //Note on channel 1 (0x90), some note value (note), middle velocity (0x45):
    noteOn(0x90, note, 0x45);
    delay(100);
    //Note on channel 1 (0x90), some note value (note), silent velocity (0x00):
    noteOn(0x90, note, 0x00);
    delay(100);
  }
}

//  plays a MIDI note.  Doesn't check to see that
//  cmd is greater than 127, or that data values are  less than 127:
void noteOn(int cmd, int pitch, int velocity) {
  Serial.write(cmd);
  Serial.write(pitch);
  Serial.write(velocity);
}

// code stored in the sketch: MIDI_Tutorial_1.ino
#include <MIDI.h>
#include <midi_Defs.h>
#include <midi_Message.h>
#include <midi_Namespace.h>
#include <midi_Settings.h>

/*
 MIDI note player

 This sketch shows how to use the serial transmit pin (pin 1) to send MIDI note data.
 If this circuit is connected to a MIDI synth, it will play
 the notes F#-0 (0x1E) to F#-5 (0x5A) in sequence.

 The circuit:
 * digital in 1 connected to MIDI jack pin 5
 * MIDI jack pin 2 connected to ground
 * MIDI jack pin 4 connected to +5V through 220-ohm resistor
 Attach a MIDI cable to the jack, then to a MIDI synth, and play music.

 This example code is in the public domain.
 http://www.arduino.cc/en/Tutorial/Midi

 */


MIDI_CREATE_DEFAULT_INSTANCE();

void setup() {
  MIDI.begin(1);
  //  Set MIDI baud rate:
  Serial.begin(115200);
}

void loop() {
  // play notes from F#-0 (0x1E) to F#-5 (0x5A):
  for (int note = 0x1E; note < 0x5A; note ++) {

    MIDI.sendNoteOn(note,127,1);  // Send a Note (pitch note, velo 127 on channel 1)
    delay(1000);                // Wait for a second
    MIDI.sendNoteOff(note,127,1);
    
  }
}
