# Fritzing sketch Opto_Interruptor_2 (saved by Fritzing 0.9.2b)

parts:
  Arduino = Arduino Uno (Rev3)
  R1 = Resistor [tolerance=±5% resistance=220 package="0603 [SMD]"]
  Q2 = PHOTOTRANSISTOR REFLECTIVE OBJECT SENSOR [package=qrb1114-side]
  R2 = Resistor [tolerance=±5% resistance=1k package="0603 [SMD]"]
  Q4 = PHOTOTRANSISTOR REFLECTIVE OBJECT SENSOR [package=qrb1114-side]
  Q5 = PHOTOTRANSISTOR REFLECTIVE OBJECT SENSOR [package=qrb1114-side]
  Q6 = PHOTOTRANSISTOR REFLECTIVE OBJECT SENSOR [package=qrb1114-side]
  R3 = Resistor [tolerance=±5% resistance=220 package="0603 [SMD]"]
  R4 = Resistor [tolerance=±5% resistance=220 package="0603 [SMD]"]
  R5 = Resistor [tolerance=±5% resistance=220 package="0603 [SMD]"]
  R6 = Resistor [tolerance=±5% resistance=1k package="0603 [SMD]"]
  Q7 = TRANSISTOR_NPN [package=to-92]
  Q8 = TRANSISTOR_NPN [package=to-92]

nets (from the schematic view):
  N1: Arduino.A2, Q2.C, Q4.C
  N2: Arduino.A3, Q5.C, Q6.C
  N3: Arduino.D9_PWM, R2.Pin_1
  N4: Arduino.D10_PWM/SS, R6.Pin_0
  5V: R1.Pin_0, R3.Pin_0, R4.Pin_0, R5.Pin_0
  N5: R1.Pin_1, Q2.A
  GND: Q2.E, Q4.E, Q5.E, Q6.E, Q7.E, Q8.E
  N6: Q2.K, Q6.K, Q7.C
  N7: R2.Pin_0, Q7.B
  N8: Q4.A, R3.Pin_1
  N9: Q4.K, Q5.K, Q8.C
  N10: Q5.A, R5.Pin_1
  N11: Q6.A, R4.Pin_1
  N12: R6.Pin_1, Q8.B

// code stored in the sketch: Interruptor_4_Uno.ino
/* 
* 2x2 matrix of Interruptors
* At this point most of this code is pulled directly from AccordionMega's code.
*/

int ANALOG_ROW1 = 2;//00000100
//int ANALOG_ROW2 = 3;
char DIGITAL_COLUMNS[] = { 9, 10 };

//Note: in this example we're only using two bits from each byte
int KeysStatus[] = {  
  B0000000,
  B0000000
};

//this is the value of all pins from the analog port (7 and 6 don't exist on UNO)
//B00000000
//B76543210
byte reg_values = 0;

void setup()
{
    Serial.begin(9600);
    //Digital pins start turned off
    for (int i=0; i<sizeof(DIGITAL_COLUMNS);i++){ 
        pinMode(DIGITAL_COLUMNS[i],OUTPUT);
        digitalWrite(DIGITAL_COLUMNS[i], LOW);
    }

    //PortC as input 
    DDRC = B00000000;
    //Turn on pullup resistors
    PORTC = B11111111;
}

void loop()
{
  for (int i=0; i<sizeof(DIGITAL_COLUMNS);i++){ 
    //I wonder if we can replace this with direct port write for speed?
    digitalWrite(DIGITAL_COLUMNS[i], HIGH);
    delayMicroseconds(7000);//TODO - play around with this number a bit

    //delay(500);
    
    //PINB = 8-13 (14/15 don't work), PINC = analog 0-5 (6/7 don't work), PIND = 0-7
    reg_values = ~PINC;
//    Serial.println(" ");
//    Serial.print(" Previous Values for group ");
//    Serial.print(i);
//    Serial.print(": ");
//    Serial.println(KeysStatus[i], BIN);
//    Serial.print(" Values Read: ");
//    Serial.println(reg_values, BIN);
    
    
    digitalWrite(DIGITAL_COLUMNS[i], LOW);

    if (reg_values != KeysStatus[i]){
      if (reg_values > KeysStatus[i]){             
        check_key(reg_values ^ KeysStatus[i],i,true);  //sending modified bits only
      }
      else {
        check_key(reg_values ^ KeysStatus[i],i,false); //sending modified bits only
      }           
    }
  }
}

void check_key(int reg, int group, boolean up){
   // saving 4 iterations, dividing byte by 2
   if (reg & 0xF0) {
     for(int i=0; i<4; i++){
       if ((reg >> 4+i) & 1){
         note_midi(group,i+4,up);
       }
     }
   }
   else if (reg & 0x0F) { 
    for(int i=0; i<4; i++){
       if ((reg >> i) & 1){
         note_midi(group,i,up);
       }
     }     
   }
}

//The right two most bits turn on because those pins don't exist on the Uno
const char right_notes_midi_numbers[][8] = {
  {60,59,58,57,56,55},//54,53},
  {68,67,66,65,64,63},//62,61},
  {76,75,74,73,72,71,70,69},
  {84,83,82,81,80,79,78,77},
  {92,91,90,89,88,87,86,85},
  {0,0,0,0,0,0,0,93}
};

byte midi_channel1 = 0;
byte midi_channel2 = 1;
char notes_to_play;

void note_midi(int group, int position, boolean on){
  int pitch;
  String str_warn;
  char midi_cmd;
  char curr_register = 0;
  int midi_vel;

  pitch = right_notes_midi_numbers[group][position];
  curr_register = 0;

  if(on) {
    str_warn = "Note on ";
    midi_cmd = midi_channel2 | 0x90;
    KeysStatus[group] |= (1 << position);  //setting bit value
    Serial.print(" Changed Status: ");
    Serial.println(KeysStatus[group], BIN);
    midi_vel = 127;
  }
  else if(~on) {
    str_warn = "Note off ";
    midi_cmd = midi_channel2 | 0x80;
    KeysStatus[group] &= ~(1 << position);  //setting bit value
    Serial.print(" Changed Status: ");
    Serial.println(KeysStatus[group], BIN);
    midi_vel = 0;
  }
    
  Serial.print(str_warn);
  Serial.print(pitch,DEC);
  Serial.print(" Vel: ");
  Serial.println(midi_vel);
  Serial.print(" Group: ");
  Serial.println(group);
  Serial.print(" Position: ");
  Serial.println(position);
  
  notes_to_play = right_notes_midi_numbers[group][position];
  if (notes_to_play){
    //TODO - replace with ArduinoMIDI library command
    //Serial1.print(midi_cmd, BYTE);
    //Serial1.print(notes_to_play, BYTE);
    //Serial1.print(midi_vel, BYTE);
    Serial.print(" ");
    Serial.println(notes_to_play,DEC);
  }

}

// code stored in the sketch: Interruptor_Tutorial_1.ino
/* Analog Read Interrupter
* -----------------------
*/

int ruptPin = 2; // select the input pin for the interrupter
//int ruptPin = 16; // same as A2
int val = -1; // variable to store the value coming from the sensor

void setup()
{
    Serial.begin(9600); // set up Serial library at 9600 bps
    //pinMode(ruptPin,INPUT_PULLUP);
}

void loop()
{
    val = analogRead(ruptPin); // read the value from the sensor
    Serial.println(val); // print the sensor value to the serial monitor
    delay(500);
}

// code stored in the sketch: Interruptor_Tutorial_2.ino
/* 
* 2x2 matrix of Interruptors
* At this point most of this code is pulled directly from AccordionMega's code.
*/

int ANALOG_ROW1 = 2;//00000100
int ANALOG_ROW2 = 3;
char DIGITAL_COLUMNS[] = { 9, 10 };

int analog_val_1 = -1;
int analog_val_2 = -1;

//Note: in this example we're only using two bits from each byte
int KeysStatus[] = {  
  B0000000,
  B0000000
};

//this is the value of all pins from the analog port (7 and 6 don't exist on UNO)
//B00000000
//B76543210
byte reg_values = 0;

void setup()
{
    Serial.begin(9600);
    //Digital pins start turned off
    for (int i=0; i<sizeof(DIGITAL_COLUMNS);i++){ 
        pinMode(DIGITAL_COLUMNS[i],OUTPUT);
        digitalWrite(DIGITAL_COLUMNS[i], LOW);
    }

    //PortC as input 
    DDRC = B00000000;
    //Turn on pullup resistors
    PORTC = B11111111;
}

void loop()
{
  for (int i=0; i<sizeof(DIGITAL_COLUMNS);i++){ 
    //I wonder if we can replace this with direct port write for speed?
    digitalWrite(DIGITAL_COLUMNS[i], HIGH);
    delayMicroseconds(500);//TODO - play around with this number a bit

    delay(500);
    
    //PINB = 8-13 (14/15 don't work), PINC = analog 0-5 (6/7 don't work), PIND = 0-7
    reg_values = ~PINC;
    Serial.println(" ");
    Serial.print(" Previous Values for group ");
    Serial.print(i);
    Serial.print(": ");
    Serial.println(KeysStatus[i], BIN);
    Serial.print(" Values Read: ");
    Serial.println(reg_values, BIN);
    
    
    digitalWrite(DIGITAL_COLUMNS[i], LOW);

    if (reg_values != KeysStatus[i]){
      if (reg_values > KeysStatus[i]){             
        check_key(reg_values ^ KeysStatus[i],i,true);  //sending modified bits only
      }
      else {
        check_key(reg_values ^ KeysStatus[i],i,false); //sending modified bits only
      }           
    }
  }
}

void check_key(int reg, int group, boolean up){
   // saving 4 iterations, dividing byte by 2
   if (reg & 0xF0) {
     for(int i=0; i<4; i++){
       if ((reg >> 4+i) & 1){
         note_midi(group,i+4,up);
       }
     }
   }
   else if (reg & 0x0F) { 
    for(int i=0; i<4; i++){
       if ((reg >> i) & 1){
         note_midi(group,i,up);
       }
     }     
   }
}

const char right_notes_midi_numbers[][8] = {
  {60,59,58,57,56,55,54,53},
  {68,67,66,65,64,63,62,61},
  {76,75,74,73,72,71,70,69},
  {84,83,82,81,80,79,78,77},
  {92,91,90,89,88,87,86,85},
  {0,0,0,0,0,0,0,93}
};

byte midi_channel1 = 0;
byte midi_channel2 = 1;
char notes_to_play;

void note_midi(int group, int position, boolean on){
  int pitch;
  String str_warn;
  char midi_cmd;
  char curr_register = 0;
  int midi_vel;

  pitch = right_notes_midi_numbers[group][position];
  curr_register = 0;

  if(on) {
    str_warn = "Note on ";
    midi_cmd = midi_channel2 | 0x90;
    KeysStatus[group] |= (1 << position);  //setting bit value
    Serial.print(" Changed Status: ");
    Serial.println(KeysStatus[group], BIN);
    midi_vel = 127;
  }
  else if(~on) {
    str_warn = "Note off ";
    midi_cmd = midi_channel2 | 0x80;
    KeysStatus[group] &= ~(1 << position);  //setting bit value
    Serial.print(" Changed Status: ");
    Serial.println(KeysStatus[group], BIN);
    midi_vel = 0;
  }
    
  Serial.print(str_warn);
  Serial.print(pitch,DEC);
  Serial.print(" Vel: ");
  Serial.println(midi_vel);
  Serial.print(" Group: ");
  Serial.println(group);
  Serial.print(" Position: ");
  Serial.println(position);
  
  notes_to_play = right_notes_midi_numbers[group][position];
  if (notes_to_play){
    //TODO - replace with ArduinoMIDI library command
    //Serial1.print(midi_cmd, BYTE);
    //Serial1.print(notes_to_play, BYTE);
    //Serial1.print(midi_vel, BYTE);
    Serial.print(" ");
    Serial.println(notes_to_play,DEC);
  }

}

// code stored in the sketch: MIDI Tutorial.ino
/*
 MIDI note player

 This sketch shows how to use the serial transmit pin (pin 1) to send MIDI note data.
 If this circuit is connected to a MIDI synth, it will play
 the notes F#-0 (0x1E) to F#-5 (0x5A) in sequence.


 The circuit:
 * digital in 1 connected to MIDI jack pin 5
 * MIDI jack pin 2 connected to ground
 * MIDI jack pin 4 connected to +5V through 220-ohm resistor
 Attach a MIDI cable to the jack, then to a MIDI synth, and play music.

 created 13 Jun 2006
 modified 13 Aug 2012
 by Tom Igoe

 This example code is in the public domain.

 http://www.arduino.cc/en/Tutorial/Midi

 */

void setup() {
  //  Set MIDI baud rate:
  Serial.begin(31250);
}

void loop() {
  // play notes from F#-0 (0x1E) to F#-5 (0x5A):
  for (int note = 0x1E; note < 0x5A; note ++) {
    //Note on channel 1 (0x90), some note value (note), middle velocity (0x45):
    noteOn(0x90, note, 0x45);
    delay(100);
    //Note on channel 1 (0x90), some note value (note), silent velocity (0x00):
    noteOn(0x90, note, 0x00);
    delay(100);
  }
}

//  plays a MIDI note.  Doesn't check to see that
//  cmd is greater than 127, or that data values are  less than 127:
void noteOn(int cmd, int pitch, int velocity) {
  Serial.write(cmd);
  Serial.write(pitch);
  Serial.write(velocity);
}

// code stored in the sketch: MIDI_Tutorial_1.ino
#include <MIDI.h>
#include <midi_Defs.h>
#include <midi_Message.h>
#include <midi_Namespace.h>
#include <midi_Settings.h>

/*
 MIDI note player

 This sketch shows how to use the serial transmit pin (pin 1) to send MIDI note data.
 If this circuit is connected to a MIDI synth, it will play
 the notes F#-0 (0x1E) to F#-5 (0x5A) in sequence.

 The circuit:
 * digital in 1 connected to MIDI jack pin 5
 * MIDI jack pin 2 connected to ground
 * MIDI jack pin 4 connected to +5V through 220-ohm resistor
 Attach a MIDI cable to the jack, then to a MIDI synth, and play music.

 This example code is in the public domain.
 http://www.arduino.cc/en/Tutorial/Midi

 */


MIDI_CREATE_DEFAULT_INSTANCE();

void setup() {
  MIDI.begin(1);
  //  Set MIDI baud rate:
  Serial.begin(115200);
}

void loop() {
  // play notes from F#-0 (0x1E) to F#-5 (0x5A):
  for (int note = 0x1E; note < 0x5A; note ++) {

    MIDI.sendNoteOn(note,127,1);  // Send a Note (pitch note, velo 127 on channel 1)
    delay(1000);                // Wait for a second
    MIDI.sendNoteOff(note,127,1);
    
  }
}
