# Fritzing sketch Power_Tutorial (saved by Fritzing 0.9.2b)

parts:
  Part1 = Arduino Uno (Rev3)
  S1 = Toggle Switch [package=THT]
  VCC1 = Battery
  LED1 = LED - 3mm [color="Red (633nm)" package="3 mm [THT]"]
  R1 = Resistor [tolerance=±5% resistance=330 package="0805 [SMD]"]

nets:
  N1: Part1.GND, VCC1.-, R1.Pin_1
  N2: Part1.5V, LED1.anode
  N3: Part1.VIN, S1.L2
  N4: S1.COM, VCC1.+
  N5: LED1.cathode, R1.Pin_0
